// Logisim project projetofinal.circ as structural Verilog: 1 circuit, main circuit main
module main (
  input  in_1,
  output out_2,
  output out_3,
  output out_4
);

  wire and_1_out, and_2_out, and_3_out, and_4_out, and_5_out, and_6_out, and_7_out, and_8_out, and_9_out,
       and_10_out, and_11_out, and_12_out, and_13_out, button_1_out, button_2_out, j_k_ff_1_q, j_k_ff_3_q,
       not_1_out, not_2_out, not_3_out, not_4_out, not_5_out, not_6_out, not_7_out, not_8_out, not_9_out,
       not_10_out, not_11_out, not_12_out, or_1_out, or_2_out, or_3_out, or_4_out, or_5_out, or_6_out,
       or_7_out, or_8_out;

  Button button_1 (.out(button_1_out));
  Button button_2 (.out(button_2_out));
  or or_1 (or_1_out, button_1_out, and_1_out);
  and and_1 (and_1_out, j_k_ff_1_q, or_2_out);
  J_K_Flip_Flop j_k_ff_1 (.J(in_1), .clk(button_2_out), .K(in_1), .Q(j_k_ff_1_q));  // open: Qn, preset, en, reset
  J_K_Flip_Flop j_k_ff_2 (.J(in_1), .clk(or_1_out), .K(in_1), .Q(out_3));  // open: Qn, preset, en, reset
  not not_1 (not_1_out, out_3);
  not not_2 (not_2_out, out_2);
  not not_3 (not_3_out, out_4);
  and and_2 (and_2_out, out_4, out_3);
  and and_3 (and_3_out, out_4, not_1_out, not_2_out);
  or or_2 (or_2_out, and_3_out, and_4_out);
  and and_4 (and_4_out, not_3_out, out_3, out_2);
  and and_5 (and_5_out, out_3, j_k_ff_3_q);
  J_K_Flip_Flop j_k_ff_3 (
    .J(and_2_out), .clk(or_1_out), .K(out_3), .Q(j_k_ff_3_q), .Qn(out_2));  // open: preset, en, reset
  not not_4 (not_4_out, out_3);
  not not_5 (not_5_out, out_2);
  not not_6 (not_6_out, out_4);
  not not_7 (not_7_out, out_3);
  not not_8 (not_8_out, out_2);
  not not_9 (not_9_out, out_4);
  not not_10 (not_10_out, out_3);
  not not_11 (not_11_out, out_3);
  not not_12 (not_12_out, out_2);
  J_K_Flip_Flop j_k_ff_4 (.J(and_5_out), .clk(or_1_out), .K(out_3), .Qn(out_4));  // open: Q, preset, en, reset
  and and_6 (and_6_out, out_4, not_4_out, not_5_out);
  and and_7 (and_7_out, not_6_out, not_7_out, out_2);
  and and_8 (and_8_out, out_4, out_3, not_8_out);
  and and_9 (and_9_out, not_9_out, out_3, out_2);
  and and_10 (and_10_out, out_4, out_3, out_2);
  and and_11 (and_11_out, out_4, not_10_out, out_2);
  and and_12 (and_12_out, not_11_out, not_12_out);
  and and_13 (and_13_out, out_2, out_3);
  or or_3 (or_3_out, and_7_out, or_4_out);
  or or_4 (or_4_out, and_8_out, and_9_out);
  or or_5 (or_5_out, and_12_out, or_3_out);
  or or_6 (or_6_out, and_13_out, and_6_out);
  or or_7 (or_7_out, or_6_out, and_11_out);
  LED led_1 (.in(or_8_out));
  or or_8 (or_8_out, or_7_out, and_10_out);
  LED led_2 (.in(and_7_out));
  LED led_3 (.in(and_8_out));
  LED led_4 (.in(or_5_out));
  LED led_5 (.in(and_10_out));
  LED led_6 (.in(and_11_out));
  LED led_7 (.in(and_11_out));
  LED led_8 (.in(and_10_out));
  LED led_9 (.in(or_5_out));
  LED led_10 (.in(and_7_out));
  LED led_11 (.in(and_8_out));
  LED led_12 (.in(or_8_out));
  LED led_13 (.in(and_7_out));
  LED led_14 (.in(or_8_out));
  LED led_15 (.in(and_8_out));
  LED led_16 (.in(or_5_out));
  LED led_17 (.in(and_11_out));
  LED led_18 (.in(and_10_out));

  // Notes on the sheet:
  //   Botão Normal
  //   Botão Emergência
  //   ESQUERDA
  //   DIREITA
  //   CIMA
  //   BAIXO
  //   verde
  //   vermelho
  //   amarelo
  //   verde
  //   vermelho
  //   amarelo
  //            CIMA
  //                       ESQUERDA
  //   DIREITA
  //   BAIXO
endmodule
