// Logisim project Trabalho SD (Tiago, Tomas, Joao) Turma 2.circ as structural Verilog: 1 circuit, main circuit main
module main (
  input  in_1,
  output out_2,
  output out_3
);

  wire button_1_out, j_k_ff_1_q, j_k_ff_2_q, j_k_ff_2_qn;

  Button button_1 (.out(button_1_out));
  J_K_Flip_Flop j_k_ff_1 (
    .J(j_k_ff_2_qn), .clk(button_1_out), .K(in_1), .Q(j_k_ff_1_q));  // open: Qn, preset, en, reset
  or or_1 (out_2, j_k_ff_2_q, j_k_ff_1_q);
  J_K_Flip_Flop j_k_ff_2 (
    .J(j_k_ff_1_q), .clk(button_1_out), .K(in_1), .Q(j_k_ff_2_q), .Qn(j_k_ff_2_qn));  // open: preset, en, reset
  nor nor_1 (out_3, j_k_ff_1_q, j_k_ff_1_q);

  // Notes on the sheet:
  //   Membros: Tiago Estrela 20220534
  //   Tomás Salgueiro 20220589
  //   João Moniz 20220550
endmodule
